// Logisim project Project1Given.circ as structural Verilog: 4 circuits, main circuit main
module main (
  input  in_1,
  input  in_2,
  input  in_3,
  input  in_4,
  input  Five,
  output N,
  output E,
  output [3:0] out_8
);

  wire fiveseven_1_a, fiveseven_1_b, fiveseven_1_c, fiveseven_1_d, fiveseven_1_e, fiveseven_1_f,
       fiveseven_1_g;

  Compare compare_1 (
    .Y1(1'b1), .Y2(1'b0), .Test(1'b1), .in_8(1'b1), .in_9(1'b1), .in_10(1'b1), .N(N), .E(E));  // open: X0, X1, X2, Y0, in_11, in_12, in_13, in_14
  Gray gray_1 (.B0(1'b1), .B1(1'b0), .B2(1'b1), .B3(1'b1), .G0(out_8[0]), .G1(out_8[1]), .G2(out_8[2]), .G3(out_8[3]));
  FiveSeven fiveseven_1 (
    .V(in_2), .W(in_2), .X(in_3), .Y(in_4), .Z(in_4), .in_7(Five), .A(fiveseven_1_a), .B(fiveseven_1_b),
    .C(fiveseven_1_c), .D(fiveseven_1_d), .E(fiveseven_1_e), .F(fiveseven_1_f), .G(fiveseven_1_g));  // open: in_10, in_12, in_11, in_13, in_9, in_6, in_8
  _7_Segment_Display u_7_segment_display_1 (
    .g(fiveseven_1_g), .f(fiveseven_1_f), .a(fiveseven_1_a), .b(fiveseven_1_b), .e(fiveseven_1_e),
    .d(fiveseven_1_d), .c(fiveseven_1_c));  // open: dp
endmodule

module Compare (
  input  X0,
  input  X1,
  input  X2,
  input  Y0,
  input  Y1,
  input  Y2,
  input  Test,
  input  in_8,
  input  in_9,
  input  in_10,
  input  in_11,
  input  in_12,
  input  in_13,
  input  in_14,
  output N,
  output E
);

  wire and_2_out, and_3_out, and_4_out, EQUAL1, EQUAL2, nand_1_out, nand_2_out, nand_3_out, nand_4_out,
       not_1_out, not_2_out, not_3_out, TRUE1, TRUE2, TRUE3, xnor_1_out, xnor_2_out, xnor_3_out;

  not not_1 (not_1_out, X2);
  not not_2 (not_2_out, X1);
  not not_3 (not_3_out, X0);
  nand nand_1 (nand_1_out, Test, in_8, in_9);
  nand nand_2 (nand_2_out, in_10, in_11);
  nand nand_3 (nand_3_out, in_12, in_13, in_14);
  xnor xnor_1 (xnor_1_out, X0, Y0);
  xnor xnor_2 (xnor_2_out, X1, Y1);
  xnor xnor_3 (xnor_3_out, X2, Y2);
  or or_1 (N, TRUE1, TRUE2, TRUE3);
  and and_1 (TRUE1, not_1_out, Y2);
  xnor xnor_4 (EQUAL1, X2, Y2);
  and and_2 (and_2_out, not_2_out, Y1);
  xnor xnor_5 (EQUAL2, X1, Y1);
  and and_3 (and_3_out, not_3_out, Y0);
  and and_4 (and_4_out, nand_1_out, nand_3_out);
  and and_5 (TRUE2, EQUAL1, and_2_out);
  and and_6 (TRUE3, EQUAL1, EQUAL2, and_3_out);
  LED led_1 (.in(and_4_out));
  nand nand_4 (nand_4_out, nand_1_out, nand_2_out, nand_3_out);
  and and_7 (E, xnor_1_out, xnor_2_out, xnor_3_out);

  // Other names for the same wires on the sheet: CX0 = X0; CX1 = X1; CX2 = X2; CY0 = Y0; CY1 = Y1; CY2 = Y2;
  //   E_Output = E; N_Output = N

  // Notes on the sheet:
  //   E_Output
  //   N_Output
endmodule

module Gray (
  input  B0,
  input  B1,
  input  B2,
  input  B3,
  output G0,
  output G1,
  output G2,
  output G3
);

  wire and_1_out, and_2_out, and_3_out, and_4_out, and_5_out, and_6_out, not_2_out, not_3_out, not_4_out,
       not_5_out, not_6_out, not_7_out;

  not not_1 (G1, B2);
  xnor xnor_1 (G0, B0, B1);
  not not_2 (not_2_out, B1);
  not not_3 (not_3_out, B2);
  not not_4 (not_4_out, B3);
  not not_5 (not_5_out, B1);
  not not_6 (not_6_out, B2);
  not not_7 (not_7_out, B3);
  and and_1 (and_1_out, B1, not_4_out);
  and and_2 (and_2_out, B2, not_4_out);
  and and_3 (and_3_out, not_2_out, not_3_out, B3);
  and and_4 (and_4_out, not_5_out, B3);
  and and_5 (and_5_out, B1, B2, not_7_out);
  and and_6 (and_6_out, not_6_out, B3);
  or or_1 (G2, and_1_out, and_2_out, and_3_out);
  or or_2 (G3, and_4_out, and_5_out, and_6_out);

  // Other names for the same wires on the sheet: X0 = B0; X1 = B1; X2 = B2; X3 = B3; Y0 = G0; Y1 = G1; Y2 = G2;
  //   Y3 = G3
endmodule

module FiveSeven (
  input  V,
  input  W,
  input  X,
  input  Y,
  input  Z,
  input  in_6,
  input  in_7,
  input  in_8,
  input  in_9,
  input  in_10,
  input  in_11,
  input  in_12,
  input  in_13,
  output A,
  output B,
  output C,
  output D,
  output E,
  output F,
  output G
);

  wire and_1_out, and_2_out, and_3_out, and_4_out, and_5_out, and_6_out, and_9_out, and_10_out, and_11_out,
       and_12_out, and_13_out, and_14_out, and_15_out, and_27_out, and_28_out, nor_1_out, nor_2_out,
       nor_3_out, nor_4_out, nor_5_out, nor_6_out, not_2_out, not_3_out, not_4_out, not_5_out, NOT_Z,
       or_3_out, xor_1_out, xor_2_out, xor_3_out, xor_4_out, xor_5_out, xor_6_out;
  wire [6:0] Four_Nine, One_Six;
  wire [6:1] Two_Seven, Zero_Five;
  wire [6:4] Three_Eight;
  wire [9:0] D_t;
  wire [9:7] Digit;
  wire [9:9] undriven;

  not not_1 (NOT_Z, Z);
  nor nor_1 (nor_1_out, V, W);
  nor nor_2 (nor_2_out, X, Y);
  and and_1 (and_1_out, V, W);
  and and_2 (and_2_out, X, Y);
  xor xor_1 (xor_1_out, V, W);
  nor nor_3 (nor_3_out, X, Y);
  nor nor_4 (nor_4_out, V, W);
  xor xor_2 (xor_2_out, X, Y);
  and and_3 (and_3_out, V, W);
  xor xor_3 (xor_3_out, X, Y);
  xor xor_4 (xor_4_out, V, W);
  and and_4 (and_4_out, X, Y);
  and and_5 (and_5_out, V, W);
  nor nor_5 (nor_5_out, X, Y);
  nor nor_6 (nor_6_out, V, W);
  and and_6 (and_6_out, X, Y);
  xor xor_5 (xor_5_out, V, W);
  xor xor_6 (xor_6_out, X, Y);
  and and_7 (Zero_Five[5], nor_1_out, nor_2_out);
  and and_8 (Four_Nine[6], and_1_out, and_2_out);
  and and_9 (and_9_out, xor_1_out, nor_3_out);
  and and_10 (and_10_out, nor_4_out, xor_2_out);
  and and_11 (and_11_out, and_3_out, xor_3_out);
  and and_12 (and_12_out, xor_4_out, and_4_out);
  and and_13 (and_13_out, and_5_out, nor_5_out);
  and and_14 (and_14_out, nor_6_out, and_6_out);
  and and_15 (and_15_out, xor_5_out, xor_6_out);
  or or_1 (One_Six[2], and_9_out, and_10_out);
  or or_2 (Three_Eight[6], and_11_out, and_12_out);
  or or_3 (or_3_out, and_13_out, and_14_out);
  or or_4 (Two_Seven[1], or_3_out, and_15_out);
  and and_16 (One_Six[0], One_Six[2], Z);
  and and_17 (One_Six[1], One_Six[2], NOT_Z);
  and and_18 (One_Six[3], One_Six[2], Z);
  and and_19 (One_Six[4], One_Six[2], Z);
  and and_20 (One_Six[5], One_Six[2], Z);
  and and_21 (One_Six[6], One_Six[2], Z);
  and and_22 (Three_Eight[4], Three_Eight[6], Z);
  and and_23 (Three_Eight[5], Three_Eight[6], Z);
  not not_2 (not_2_out, Two_Seven[1]);
  and and_24 (Zero_Five[1], Zero_Five[5], NOT_Z);
  and and_25 (Zero_Five[4], Zero_Five[5], NOT_Z);
  and and_26 (Zero_Five[6], Zero_Five[5], Z);
  and and_27 (and_27_out, Four_Nine[6], NOT_Z);
  and and_28 (and_28_out, Four_Nine[6], NOT_Z);
  not not_3 (not_3_out, Four_Nine[6]);
  and and_29 (Two_Seven[2], Two_Seven[1], Z);
  and and_30 (Two_Seven[3], Two_Seven[1], NOT_Z);
  and and_31 (Two_Seven[4], Two_Seven[1], NOT_Z);
  and and_32 (Two_Seven[5], Two_Seven[1], not_2_out);
  and and_33 (Two_Seven[6], Two_Seven[1], NOT_Z);
  not not_4 (not_4_out, and_27_out);
  and and_34 (Four_Nine[0], not_4_out, Four_Nine[6]);
  and and_35 (Four_Nine[3], Four_Nine[6], not_5_out);
  not not_5 (not_5_out, and_28_out);
  and and_36 (Four_Nine[4], not_3_out, Four_Nine[6]);
  assign {Digit, G, F, E, D, C, B, A} = {{3{in_7}}, Zero_Five[6:4], {2{Zero_Five[5]}}, Zero_Five[1], Zero_Five[5]} | {{3{in_11}}, One_Six} | {{3{in_13}}, Two_Seven, Two_Seven[1]} | {{3{in_12}}, Three_Eight, {4{Three_Eight[6]}}} | {{3{in_10}}, {2{Four_Nine[6]}}, Four_Nine[4:3], {2{Four_Nine[6]}}, Four_Nine[0]};  // OR_Gate or_5, 10 bits wide
  assign D_t = {10{in_6}} | {undriven[9], in_9, {8{in_8}}};  // OR_Gate or_6, 10 bits wide

  // Other names for the same wires on the sheet: Digit[6:0] = {G, F, E, D, C, B, A};
  //   Four_Nine (some bits) = {{3{in_10}}, {3{Four_Nine[6]}}}; One_Six[9:7] = {3{in_11}};
  //   Three_Eight (some bits) = {{3{in_12}}, {4{Three_Eight[6]}}}; Two_Seven (some bits) = {{3{in_13}}, Two_Seven[1]};
  //   Zero_Five (some bits) = {{3{in_7}}, {3{Zero_Five[5]}}}
endmodule
